# Fritzing sketch dum.bot (saved by Fritzing 0.9.1b)

parts:
  Raspberry_Pi1 = Raspberry Pi B rev2
  M2 = DC Motor
  TRINKET1 = Trinket 3V
  VCC1 = 4 x AAA Battery Mount
  S1 = H-Bridge with L298N
  M1 = DC Motor
  Composant1 = SRF05 Ultrasonic Rangefinder
  R1 = Resistor [tolerance=±5% resistance=1k package=THT]
  R2 = Resistor [tolerance=±5% resistance=1k package=THT]  # not connected
  R3 = Resistor [tolerance=±5% resistance=1k package=THT]

nets:
  N1: Raspberry_Pi1.GPIO_2, TRINKET1.no_name_yet#9
  N2: Raspberry_Pi1.GPIO_3, TRINKET1.no_name_yet#7
  GND: Raspberry_Pi1.GND, TRINKET1.no_name_yet#2, VCC1.-, Composant1.GND, R1.Pin_1
  N3: Raspberry_Pi1.GPIO_23, S1.IN4
  N4: Raspberry_Pi1.GPIO_14, S1.IN2
  N5: Raspberry_Pi1.GPIO_15, S1.IN3
  N6: Raspberry_Pi1.GPIO_4, S1.IN1
  N7: M2.pin_1, S1.M2-02
  N8: M2.pin_2, S1.M2-01
  N9: TRINKET1.no_name_yet#1, VCC1.+, S1.12V
  N10: TRINKET1.no_name_yet#3, R3.Pin_0
  N11: TRINKET1.no_name_yet#4, Composant1.Trig
  5V: S1.5V, Composant1.VCC
  N12: S1.ENA, S1.ENA-5V
  N13: S1.ENB, S1.ENB-5V
  N14: S1.M1-01, M1.pin_2
  N15: S1.M1-02, M1.pin_1
  N16: Composant1.Echo, R3.Pin_1

custom parts:
  Trinket 3V: Adafruit Trinket 3V
  H-Bridge with L298N: h-bridge
